# Fritzing sketch control_for_print (saved by Fritzing 0.9.2b)
circuit board: 5.99967cm x 2.76429cm
breadboards: 1

parts:
  Raspberry_Pi1 = Raspberry Pi 2
  继电器 = NPN-Transistor [package="TO92 [THT]"]
  红外 = NPN-Transistor [package="TO92 [THT]"]
  红外_2 = NPN-Transistor [package="TO92 [THT]"]

nets:
  N1: Raspberry_Pi1.GPIO20, 红外_2.C
  N2: Raspberry_Pi1.GPIO16, 红外.C
  N3: Raspberry_Pi1.GPIO12, 继电器.E
  N4: Raspberry_Pi1.GND, 继电器.C, 红外.E, 红外_2.E
  N5: Raspberry_Pi1.5V, 继电器.B, 红外.B, 红外_2.B
